# Fritzing sketch vinification-controller (saved by Fritzing 0.9.3b)
circuit board: 8.46667cm x 5.64444cm

parts:
  Q1_cooling_mosfet = MOSFET-NCHANNEL [package=to220v]
  Q2_heating_mosfet = MOSFET-NCHANNEL [package=to220v]
  J9_-_heating_connector = screw terminal, 2 pins
  J9_-_cooling_connector = screw terminal, 2 pins
  J1 = Power Jack [package=power_jack_slot]
  U1_3_3V_regulator = Voltage Regulator - 3.3V [package="TO220 [THT]"]
  Part1 = ESP-WROOM-32 [ESP-32S] Module [part_number=ESP-WROOM-32]

nets:
  N1: Q1_cooling_mosfet.G, Part1.IO23
  N2: Q1_cooling_mosfet.D, J9_-_cooling_connector.pin1
  N3: Q1_cooling_mosfet.S, Q2_heating_mosfet.S, J1.PWR, U1_3_3V_regulator.input_voltage
  N4: Q2_heating_mosfet.G, Part1.IO22
  N5: Q2_heating_mosfet.D, J9_-_heating_connector.pin1
  GND: J9_-_heating_connector.pin2, J9_-_cooling_connector.pin2, J1.GNDBREAK, U1_3_3V_regulator.GND, Part1.GND
  N6: U1_3_3V_regulator.output_voltage, Part1.3V3

custom parts:
  ESP-WROOM-32 [ESP-32S] Module: Espressif ESP-WROOM-32 WiFi/Bluetooth LE microcontroller module also known as the Ai-Thinker ESP-32S module with similar formfactor. The ESP32 is a microcontroller chip with WiFi and BLE capabilities. The chip is developed by Espressif and is the successor to the popular ESP8266 WiFi module.
